// Digital circuit Computer.dig as structural Verilog
module Computer (
  input  clk
);

  wire ALU, alu_1_p9, Carry, CLK_t, demultiplexer_1_out_0, demultiplexer_1_out_1, HLT, JMP, LD, LDCTR,
       LDREGA, not_1_out, not_2_out, or_2_out, pulldown_1_out, reset_1_out;
  wire [3:0] IBottom;
  wire [7:4] Instruction;
  wire [23:0] A, B, C, CTR, D, Data, JMPDST, ld_1_rega, ld_1_regb, REGA, REGB, REGC, REGD;

  ROM #(.bigEndian("true"), .AddrBits(24), .isProgramMemory("true"), .Bits(32)) rom_1 (
    .A(CTR), .sel(1'b1), .D({Data, Instruction, IBottom}));
  Register #(.Bits(24)) u_A (.D(REGA), .C(CLK_t), .en(LDREGA), .Q(A));
  Register #(.Bits(24)) u_B (.D(REGB), .C(CLK_t), .en(LDREGA), .Q(B));
  Register #(.Bits(24)) u_C (.D(REGC), .C(CLK_t), .en(LD), .Q(C));
  Register #(.Bits(24)) u_D (.D(REGD), .C(CLK_t), .en(LD), .Q(D));
  // Probe on CTR
  // Probe on A
  // Probe on B
  // Probe on C
  // Probe on D
  // Probe on Carry
  // Probe on CTR
  // Probe on A
  // Probe on B
  // Probe on C
  // Probe on D
  // Probe on Carry
  LD ld_1 (
    .A(A), .B(B), .C(C), .D(D), .Data(Data), .Enable(LD), .Instruction(IBottom), .REGA(ld_1_rega),
    .REGB(ld_1_regb), .REGC(REGC), .REGD(REGD));
  // Probe on {Instruction, IBottom}
  // Probe on Data
  // Probe on {Instruction, IBottom}
  // Probe on Data
  // ALU alu_1: pin names not known; wires that end beside it: ld_1_rega, ld_1_regb, Data, ALU, IBottom, Carry, REGA, REGB, alu_1_p9
  Demultiplexer demultiplexer_1 (
    .sel(not_1_out), .in(ALU), .out_0(demultiplexer_1_out_0), .out_1(demultiplexer_1_out_1));
  or or_1 (LDREGA, LD, ALU);
  RS_FF_AS rs_ff_as_1 (.S(demultiplexer_1_out_0), .R(demultiplexer_1_out_1), .Q(Carry));  // open: nQ
  not not_1 (not_1_out, alu_1_p9);
  PullDown pulldown_1 (.out(pulldown_1_out));
  JMP jmp_1 (
    .A(REGA), .B(REGB), .Data(Data), .Enable(JMP), .Instruction(IBottom), .Carry(alu_1_p9), .Counter(JMPDST),
    .JMP(LDCTR));
  Decoder #(.Selector_Bits(4)) decoder_1 (
    .sel(Instruction), .out_0(LD), .out_1(ALU), .out_2(JMP), .out_15(HLT));  // open: out_3, out_4, out_5, out_6, out_7, out_8, out_9, out_10, out_11, out_12, out_13, out_14
  Reset reset_1 (.out(reset_1_out));
  not not_2 (not_2_out, reset_1_out);
  Break break_1 (.brk(HLT));
  or or_2 (or_2_out, HLT, clk);
  or or_3 (CLK_t, or_2_out, 1'b0);
  CounterPreset #(.maxValue(4194304), .Bits(24), .isProgramCounter("true")) Program_Counter (
    .en(1'b1), .C(CLK_t), .dir(pulldown_1_out), .in(JMPDST), .ld(LDCTR), .clr(not_2_out), .out(CTR));  // open: ovf

  // Other names for the same wires on the sheet: Instruction[3:0] = IBottom; ITop[3:0] = Instruction; LDREGB = LDREGA;
  //   LDREGC = LD; LDREGD = LD

  // Notes on the sheet:
  //   clk: Hz: 100
  //   Read ROM
  //   contents of rom_1 (hex, n*v repeats v):
  //   ffffff01,ff02,ff0003,ff000000,604,ff,705,f000000a,ff000706,30a
  //   ,10*0,504
endmodule
